# Fritzing sketch blink-led-breadboard (saved by Fritzing 1.0.5)
breadboards: 1

parts:
  Part1 = Arduino Uno (Rev3)
  LED1 = LED - 5mm [color="Red (633nm)" current=0.030A package="5 mm [THT]"]
  R1 = Resistor [tolerance=±5% power=0.25W resistance=220 package=THT]

nets:
  N1: Part1.D13/SCK, R1.Pin_1
  N2: Part1.GND, LED1.cathode
  N3: LED1.anode, R1.Pin_0

// code stored in the sketch: blink-led-ino.ino
void setup() {
    // put your setup code here, to run once:
    pinMode(13, OUTPUT);
}

void loop() {
    // put your main code here, to run repeatedly:
    digitalWrite(13, HIGH);
    delay(3000);
    digitalWrite(13, LOW);
    delay(500);
}
